// Logisim project jiz119_lab7.circ as structural Verilog: 2 circuits, main circuit Multiplication
module Multiplication (
);

  wire button_1_out, CLK, clock_1_out, Done, is_1, not_1_out, not_2_out;
  wire [7:0] shifter_2_out;
  wire [7:1] Multiplier_q;
  wire [15:0] adder_1_out, Multiplicand_q, Product_2_q, shifter_1_out;

  Clock clock_1 (.out(clock_1_out));
  Button button_1 (.out(button_1_out));
  LED led_1 (.in(Done));
  or or_1 (CLK, clock_1_out, button_1_out);
  Register Multiplier (.D(shifter_2_out), .en(not_1_out), .Q({Multiplier_q, is_1}), .clk(CLK));  // open: clr
  not not_1 (not_1_out, Done);
  // Probe on {Multiplier_q, is_1}
  Register #(.width(16)) Multiplicand (.D(shifter_1_out), .en(not_2_out), .Q(Multiplicand_q), .clk(CLK));  // open: clr
  not not_2 (not_2_out, Done);
  // Probe on Multiplicand_q
  Comparator comparator_1 (.a({Multiplier_q, is_1}), .b({8{1'b0}}), .eq(Done));  // open: gt, lt
  Shifter #(.width(16)) shifter_1 (.in(Multiplicand_q), .\dist (4'b0001), .out(shifter_1_out));
  Shifter #(.shift("lr")) shifter_2 (.in({Multiplier_q, is_1}), .\dist (3'b001), .out(shifter_2_out));
  Adder #(.width(16)) adder_1 (.a(Product_2_q), .b(Multiplicand_q), .out(adder_1_out));  // open: cin, cout
  // Probe on Product_2_q
  Register #(.width(16)) Product_2 (.D(adder_1_out), .en(is_1), .Q(Product_2_q), .clk(CLK));  // open: clr
endmodule

module Division (
);

  wire button_1_out, CLK, clock_1_out, comparator_1_gt, is_1, not_1_out;
  wire [7:0] adder_1_out, adder_2_out, Dividend_2_q, Divisor_q, multiplexer_1_out, Quotient, Quotient_2_q,
       Remainder, Remainder_q, shifter_1_out, shifter_2_out, shifter_3_out, subtractor_1_out;

  // Probe on Dividend_2_q
  Register Divisor (.D(Divisor_q), .Q(Divisor_q), .clk(CLK));  // open: en, clr
  Clock clock_1 (.out(clock_1_out));
  or or_1 (CLK, clock_1_out, button_1_out);
  Button button_1 (.out(button_1_out));
  Register Dividend_2 (.D(shifter_1_out), .Q(Dividend_2_q), .clk(CLK));  // open: en, clr
  Subtractor subtractor_1 (.a(Remainder), .b(Divisor_q), .out(subtractor_1_out));  // open: bin, bout
  // Probe on Divisor_q
  not not_1 (not_1_out, comparator_1_gt);
  Comparator comparator_1 (.a(Divisor_q), .b(Remainder), .gt(comparator_1_gt));  // open: eq, lt
  Comparator #(.width(1)) comparator_2 (.a(1'b1), .b(Dividend_2_q[7]), .eq(is_1));  // open: gt, lt
  Shifter shifter_1 (.in(Dividend_2_q), .\dist (3'b001), .out(shifter_1_out));
  Multiplexer #(.width(8), .enable("false")) multiplexer_1 (
    .in0(Remainder), .in1(subtractor_1_out), .out(multiplexer_1_out), .sel(not_1_out));
  Register u_Remainder (.D(multiplexer_1_out), .Q(Remainder_q), .clk(CLK));  // open: en, clr
  // Probe on Remainder_q
  Adder adder_1 (.a(shifter_2_out), .b(8'h1), .out(adder_1_out));  // open: cin, cout
  // Probe on Quotient_2_q
  Register Quotient_2 (.D(Quotient), .Q(Quotient_2_q), .clk(CLK));  // open: en, clr
  Shifter shifter_2 (.in(Remainder_q), .\dist (3'b001), .out(shifter_2_out));
  Multiplexer #(.width(8), .enable("false")) multiplexer_2 (
    .in0(shifter_2_out), .in1(adder_1_out), .out(Remainder), .sel(is_1));
  Shifter shifter_3 (.in(Quotient_2_q), .\dist (3'b001), .out(shifter_3_out));
  Multiplexer #(.width(8), .enable("false")) multiplexer_3 (
    .in0(shifter_3_out), .in1(adder_2_out), .out(Quotient), .sel(not_1_out));
  Adder adder_2 (.a(shifter_3_out), .b(8'h1), .out(adder_2_out));  // open: cin, cout
endmodule
