// Logisim project jiz119_lab8.circ as structural Verilog
module Register_File (
  input  in_1,
  input  [15:0] Data,
  input  Write_enable,
  input  [2:0] rd,
  input  [2:0] rs,
  input  [2:0] rt,
  input  incre7,
  input  decre7
);

  wire demultiplexer_1_out0, demultiplexer_1_out1, demultiplexer_1_out2, demultiplexer_1_out3,
       demultiplexer_1_out4, demultiplexer_1_out5, demultiplexer_1_out6, demultiplexer_1_out7, or_1_out;
  wire [15:0] adder_1_out, multiplexer_1_out, multiplexer_2_out, Register_0, Register_1, Register_2,
       Register_3, Register_4, Register_5, Register_6, Register_7, rs_out, rt_out, subtractor_1_out;

  // Probe on rs_out
  // Probe on rt_out
  Demultiplexer #(.select(3), .enable("false")) demultiplexer_1 (
    .out0(demultiplexer_1_out0), .out1(demultiplexer_1_out1), .out2(demultiplexer_1_out2),
    .out3(demultiplexer_1_out3), .out4(demultiplexer_1_out4), .out5(demultiplexer_1_out5),
    .out6(demultiplexer_1_out6), .out7(demultiplexer_1_out7), .in(Write_enable), .sel(rd));
  or or_1 (or_1_out, demultiplexer_1_out7, decre7, incre7);
  Subtractor #(.width(16)) subtractor_1 (.a(Register_7), .b(16'h1), .out(subtractor_1_out));  // open: bin, bout
  Adder #(.width(16)) adder_1 (.a(Register_7), .b(16'h1), .out(adder_1_out));  // open: cin, cout
  Multiplexer #(.width(16), .enable("false")) multiplexer_1 (
    .in0(Data), .in1(subtractor_1_out), .out(multiplexer_1_out), .sel(decre7));
  Register #(.width(16)) u_Register_0 (.D(Data), .en(demultiplexer_1_out0), .Q(Register_0), .clk(in_1));  // open: clr
  Register #(.width(16)) u_Register_1 (.D(Data), .en(demultiplexer_1_out1), .Q(Register_1), .clk(in_1));  // open: clr
  Register #(.width(16)) u_Register_2 (.D(Data), .en(demultiplexer_1_out2), .Q(Register_2), .clk(in_1));  // open: clr
  Register #(.width(16)) u_Register_3 (.D(Data), .en(demultiplexer_1_out3), .Q(Register_3), .clk(in_1));  // open: clr
  Register #(.width(16)) u_Register_4 (.D(Data), .en(demultiplexer_1_out4), .Q(Register_4), .clk(in_1));  // open: clr
  Register #(.width(16)) u_Register_5 (.D(Data), .en(demultiplexer_1_out5), .Q(Register_5), .clk(in_1));  // open: clr
  Register #(.width(16)) u_Register_6 (.D(Data), .en(demultiplexer_1_out6), .Q(Register_6), .clk(in_1));  // open: clr
  Register #(.width(16)) u_Register_7 (.D(multiplexer_2_out), .en(or_1_out), .Q(Register_7), .clk(in_1));  // open: clr
  Multiplexer #(.width(16), .enable("false")) multiplexer_2 (
    .in0(multiplexer_1_out), .in1(adder_1_out), .out(multiplexer_2_out), .sel(incre7));
  Multiplexer #(.select(3), .width(16), .enable("false")) multiplexer_3 (
    .in0(Register_0), .in1(Register_1), .in2(Register_2), .in3(Register_3), .in4(Register_4),
    .in5(Register_5), .in6(Register_6), .in7(Register_7), .out(rs_out), .sel(rs));
  Multiplexer #(.select(3), .width(16), .enable("false")) multiplexer_4 (
    .in0(Register_0), .in1(Register_1), .in2(Register_2), .in3(Register_3), .in4(Register_4),
    .in5(Register_5), .in6(Register_6), .in7(Register_7), .out(rt_out), .sel(rt));

  // Other names for the same wires on the sheet: CLK = in_1; decr7 = decre7; incr7 = incre7

  // Notes on the sheet:
  //   rs read port
  //   rt read port
endmodule
