// Logisim project jiz119_proj2.circ as structural Verilog: 7 circuits, main circuit main
// ROM
module main (
  input  in_1,
  input  [15:0] in_2,
  input  [15:0] in_3,
  output [15:0] instruction
);

  wire call, CLK, halt, I_instruction, pop, push, R_instruction, ramwe, ret;
  wire [3:0] control_1__1, control_1__2, control_1__3, control_1__4;
  wire [15:0] multiplexer_1_out, PC, PC_1, pc_1_t, pc_t, RAM_out, rs_out, rt_out;

  LED led_1 (.in(halt));
  Clock u_CLK (.out(CLK));
  Multiplexer #(.width(16), .enable("false")) multiplexer_1 (
    .in0(rt_out), .in1(pc_1_t), .out(multiplexer_1_out), .sel(call));
  ROM #(.addrWidth(16), .dataWidth(16)) rom_1 (.addr(pc_t), .data(instruction));  // open: sel
  RAM #(.addrWidth(16), .dataWidth(16), .bus("separate")) ram_1 (
    .addr(rs_out), .din(multiplexer_1_out), .data(RAM_out), .str(ramwe), .clk(CLK));  // open: sel, ld, clr
  Decoder #(.enable("false")) decoder_1 (.out0(R_instruction), .out1(I_instruction), .sel(instruction[15]));
  PC u_pc_1 (
    .Halt(halt), .CLK(CLK), .Jump_Choice(in_1), .Branch_Offset(in_2), .ret(ret), .jr(ret),
    .Straight_target(in_3), .PC(PC), .PC_1(PC_1));
  Hex_Digit_Display hex_digit_display_1 (.value(control_1__4));  // open: dp
  Hex_Digit_Display hex_digit_display_2 (.value(control_1__3));  // open: dp
  Hex_Digit_Display hex_digit_display_3 (.value(control_1__2));  // open: dp
  Control control_1 (
    .CLK(CLK), .imm(instruction[10:3]), .RAM(RAM_out), .I_type(I_instruction), .rs(instruction[8:6]),
    .rd(instruction[2:0]), .rt(instruction[5:3]), .I_instruction(I_instruction),
    .R_instruction(R_instruction), ._4(control_1__4), ._3(control_1__3), ._2(control_1__2),
    ._1(control_1__1), .opcodeR(instruction[13:9]), .opcodeI(instruction[14:11]), .call(call), .ret(ret),
    .memwe(ramwe), .halt(halt), .push(push), .pop(pop), .rs_out(rs_out), .rt_out(rt_out), .pc(pc_t),
    .pc_1(pc_1_t));
  Hex_Digit_Display hex_digit_display_4 (.value(control_1__1));  // open: dp

  // Other names for the same wires on the sheet: rd[2:0] = instruction[2:0]; imm[7:0] = instruction[10:3];
  //   rt[2:0] = instruction[5:3]; rs[2:0] = instruction[8:6]; opcodeR[4:0] = instruction[13:9];
  //   opcodeI[3:0] = instruction[14:11]

  // Notes on the sheet:
  //   contents of rom_1 (hex, n*v repeats v):
  //   8568 8ef0 8779 8df1 1a08 800 200 a00 200 8050 80a1 1a08 a02 280 1c08 a02 280
endmodule

// Reg
module Register_file (
  input  I_type,
  input  CLK,
  input  [15:0] Data,
  input  li,
  input  [2:0] rd,
  input  [2:0] rs,
  input  [2:0] rt,
  input  incr7,
  input  decr7,
  output [15:0] rs_out,
  output [15:0] rt_out
);

  wire demultiplexer_1_out0, demultiplexer_1_out1, demultiplexer_1_out2, demultiplexer_1_out3,
       demultiplexer_1_out4, demultiplexer_1_out5, demultiplexer_1_out6, or_1_out, r7W;
  wire [15:0] add, adder_1_out, multiplexer_3_out, multiplexer_4_out, multiplexer_6_out, multiplexer_7_out,
       r0, r1, r2, r3, r4, r5, r6, r7, r7G, rs_out_t, sub, subtractor_1_out, subtractor_2_out;

  Demultiplexer #(.select(3), .enable("false")) demultiplexer_1 (
    .out0(demultiplexer_1_out0), .out1(demultiplexer_1_out1), .out2(demultiplexer_1_out2),
    .out3(demultiplexer_1_out3), .out4(demultiplexer_1_out4), .out5(demultiplexer_1_out5),
    .out6(demultiplexer_1_out6), .out7(r7W), .in(1'b1), .sel(rd));
  Multiplexer #(.select(3), .width(16), .enable("false")) multiplexer_1 (
    .in0(r0), .in1(r1), .in2(r2), .in3(r3), .in4(r4), .in5(r5), .in6(r6), .in7(r7), .out(rs_out_t), .sel(rs));
  Multiplexer #(.select(3), .width(16), .enable("false")) multiplexer_2 (
    .in0(r0), .in1(r1), .in2(r2), .in3(r3), .in4(r4), .in5(r5), .in6(r6), .in7(r7), .out(rs_out), .sel(rt));
  Register #(.width(16)) u_r0 (.D(Data), .en(demultiplexer_1_out0), .Q(r0), .clk(CLK));  // open: clr
  Register #(.width(16)) u_r1 (.D(Data), .en(demultiplexer_1_out1), .Q(r1), .clk(CLK));  // open: clr
  Register #(.width(16)) u_r2 (.D(Data), .en(demultiplexer_1_out2), .Q(r2), .clk(CLK));  // open: clr
  Register #(.width(16)) u_r3 (.D(Data), .en(demultiplexer_1_out3), .Q(r3));  // open: clk, clr
  Register #(.width(16)) u_r4 (.D(Data), .en(demultiplexer_1_out4), .Q(r4));  // open: clk, clr
  Register #(.width(16)) u_r5 (.D(Data), .en(demultiplexer_1_out5), .Q(r5));  // open: clk, clr
  Register #(.width(16)) u_r6 (.D(Data), .en(demultiplexer_1_out6), .Q(r6));  // open: clk, clr
  Adder #(.width(16)) adder_1 (.a(r7G), .b(16'h1), .out(adder_1_out));  // open: cin, cout
  Multiplexer #(.width(16), .enable("false")) multiplexer_3 (
    .in0(add), .in1(sub), .out(multiplexer_3_out), .sel(incr7));
  Multiplexer #(.select(3), .width(16), .enable("false")) multiplexer_4 (
    .in0(r0), .in1(r1), .in2(r2), .in3(r3), .in4(r4), .in5(r5), .in6(r6), .in7(r7), .out(multiplexer_4_out),
    .sel(rd));
  Multiplexer #(.width(16), .enable("false")) multiplexer_5 (.in0(r7), .in1(adder_1_out), .out(add), .sel(incr7));
  Multiplexer #(.width(16), .enable("false")) multiplexer_6 (
    .in0(Data), .in1(multiplexer_3_out), .out(multiplexer_6_out), .sel(incr7));
  or or_1 (or_1_out, r7W, incr7, decr7);
  Multiplexer #(.width(16), .enable("false")) multiplexer_7 (
    .in0(multiplexer_6_out), .in1(multiplexer_3_out), .out(multiplexer_7_out), .sel(decr7));
  Register #(.width(16)) u_r7 (.D(multiplexer_7_out), .en(or_1_out), .Q(r7G), .clk(CLK));  // open: clr
  Multiplexer #(.width(16), .enable("false")) multiplexer_8 (
    .in0(rs_out_t), .in1(multiplexer_4_out), .out(rs_out), .sel(I_type));
  Subtractor #(.width(16)) subtractor_1 (.a(r7G), .b(16'h1), .out(subtractor_1_out));  // open: bin, bout
  Multiplexer #(.width(16), .enable("false")) multiplexer_9 (.in0(r7), .in1(subtractor_1_out), .out(sub), .sel(decr7));
  Subtractor #(.width(16)) subtractor_2 (.a(r7G), .b(16'h1), .out(subtractor_2_out));  // open: bin, bout
  Multiplexer #(.width(16), .enable("false")) multiplexer_10 (.in0(r7G), .in1(subtractor_2_out), .out(r7), .sel(decr7));

  assign rt_out = rs_out;
endmodule

module PC (
  input  Halt,
  input  CLK,
  input  Jump_Choice,
  input  [15:0] Branch_Offset,
  input  ret,
  input  jr,
  input  [15:0] Straight_target,
  output [15:0] PC,
  output [15:0] PC_1
);

  wire not_1_out;
  wire [15:0] Branch_Target, multiplexer_1_out, multiplexer_2_out, multiplexer_3_out;

  Multiplexer #(.width(16), .enable("false")) multiplexer_1 (
    .in0(PC_1), .in1(Branch_Target), .out(multiplexer_1_out), .sel(Jump_Choice));
  Multiplexer #(.width(16), .enable("false")) multiplexer_2 (
    .in0(multiplexer_3_out), .in1(Straight_target), .out(multiplexer_2_out), .sel(jr));
  Multiplexer #(.width(16), .enable("false")) multiplexer_3 (
    .in0(multiplexer_1_out), .in1(Straight_target), .out(multiplexer_3_out), .sel(ret));
  Register #(.width(16)) PC_register (.D(multiplexer_2_out), .en(not_1_out), .Q(PC), .clk(CLK));  // open: clr
  not not_1 (not_1_out, Halt);
  Adder #(.width(16)) adder_1 (.a(PC), .b(16'h1), .out(PC_1));  // open: cin, cout
  Adder #(.width(16)) adder_2 (.a(PC_1), .b(Branch_Offset), .out(Branch_Target));  // open: cin, cout

  // Other names for the same wires on the sheet: Brach_Offset[15:0] = Branch_Offset
endmodule

// Display
module Display_Unit (
  input  CLK,
  input  [15:0] Data,
  input  WE,
  input  Clear,
  output [3:0] _4,
  output [3:0] _3,
  output [3:0] _2,
  output [3:0] _1
);

  wire multiplexer_2_out;
  wire [15:0] multiplexer_1_out;

  Multiplexer #(.width(16), .enable("false")) multiplexer_1 (
    .in0(Data), .in1({16{1'b0}}), .out(multiplexer_1_out), .sel(Clear));
  Multiplexer #(.enable("false")) multiplexer_2 (.in0(WE), .in1(1'b1), .out(multiplexer_2_out), .sel(Clear));
  Register #(.width(16)) register_1 (
    .D(multiplexer_1_out), .en(multiplexer_2_out), .Q({_4, _3, _2, _1}), .clk(CLK));  // open: clr

  // Other names for the same wires on the sheet: clock = CLK
endmodule

module Control (
  input  CLK,
  input  [7:0] imm,
  input  [15:0] RAM,
  input  I_type,
  input  [2:0] rs,
  input  [2:0] rd,
  input  [2:0] rt,
  input  I_instruction,
  input  R_instruction,
  input  [3:0] opcodeI,
  input  [4:0] opcodeR,
  output call,
  output ret,
  output memwe,
  output halt,
  output push,
  output pop,
  output [3:0] _3,
  output [3:0] _2,
  output [3:0] _4,
  output [3:0] _1,
  output [15:0] rs_out,
  output [15:0] rt_out,
  output [15:0] pc,
  output [15:0] pc_1
);

  wire add, addF, adi, \and , andF, ani, b, beq, bez, bge, blt, bne, bnz, check_rt, clr, cmp,
       comparator_1_eq, comparator_2_gt, comparator_2_lt, cpi, decr7, Flag_Enable, incr7, jr, ld, li, lui,
       mac, mfhi, mflo, mov, mul, Negative, NF, \not , \or , or_4_out, or_14_out, or_15_out, orF, ori, put,
       shl, shlF, shr, shrF, sli, sri, st, sub, subF, zero, ZF;
  wire [2:0] multiplexer_17_out, multiplexer_19_out, Operation;
  wire [3:0] priority_encoder_2_out, priority_encoder_3_out;
  wire [15:0] B_input, b_out, beq_out, bez_out, bge_out, blt_out, bne_out, bnz_out, call_out, Data2, Data3,
       Data4, extender_1_output, extender_2_output, extender_3_output, extender_5_output, extender_6_output,
       extender_7_output, extender_8_output, extender_9_output, Go_B, high, imm_t, m_high, m_low,
       multiplexer_1_out, multiplexer_4_out, multiplexer_5_out, multiplexer_15_out, multiplexer_16_out,
       multiplexer_18_out, multiplexer_20_out, or_5_out, PC_branchoffset, result, shifter_1_out;
  wire [31:0] mac_value;

  Extender extender_1 (.immediate(Data2), .\output (extender_1_output));
  Extender extender_2 (.immediate(Data2), .\output (extender_2_output));
  Extender extender_3 (.immediate(Data2), .\output (extender_3_output));
  Extender extender_4 (.immediate(Data2), .\output (call_out));
  or or_1 (memwe, push, st, call);
  assign Data2 = {{8{1'b0}}, imm};  // Bit_Extender bit_extender_1
  Demultiplexer #(.select(5), .enable("false")) demultiplexer_1 (
    .out0(halt), .out1(put), .out2(clr), .out3(mov), .out4(mfhi), .out5(mflo), .out6(ld), .out7(st),
    .out8(push), .out9(pop), .out10(add), .out11(sub), .out12(cmp), .out13(mul), .out14(mac), .out15(\and ),
    .out16(\or ), .out17(\not ), .out18(shl), .out19(shr), .out20(jr), .out21(ret), .in(R_instruction),
    .sel(opcodeR));  // open: out22, out23, out24, out25, out26, out27, out28, out29, out30, out31
  Multiplexer #(.width(16), .enable("false")) multiplexer_1 (
    .in0(rt_out), .in1(Go_B), .out(multiplexer_1_out), .sel(check_rt));
  Extender extender_5 (.immediate(B_input), .\output (extender_5_output));
  Multiplexer #(.width(16), .enable("false")) multiplexer_2 (
    .in0(extender_2_output), .in1({16{1'b0}}), .out(bne_out), .sel(ZF));
  Multiplexer #(.width(16), .enable("false")) multiplexer_3 (
    .in0({16{1'b0}}), .in1(extender_3_output), .out(bez_out), .sel(comparator_1_eq));
  Comparator #(.width(16)) comparator_1 (.a(rs_out), .b({16{1'b0}}), .eq(comparator_1_eq));  // open: gt, lt
  ALU_component alu_component_1 (
    .A(rs_out), .B(multiplexer_1_out), .Operation(Operation), .mac(mac), .CLK(CLK), .mac_Value(mac_value),
    .High(high), .Product_Register({m_high, m_low}), .Result(result), .Zero(zero), .Negative(Negative));
  Multiplexer #(.width(16), .enable("false")) multiplexer_4 (
    .in0(B_input), .in1(extender_5_output), .out(multiplexer_4_out), .sel(adi));
  Multiplexer #(.width(16), .enable("false")) multiplexer_5 (
    .in0(multiplexer_4_out), .in1(Data2), .out(multiplexer_5_out), .sel(ani));
  Multiplexer #(.width(16), .enable("false")) multiplexer_6 (
    .in0({16{1'b0}}), .in1(extender_1_output), .out(b_out), .sel(b));
  Demultiplexer #(.select(4), .enable("false")) demultiplexer_2 (
    .out0(li), .out1(lui), .out2(adi), .out3(ani), .out4(ori), .out5(sli), .out6(sri), .out7(cpi), .out8(b),
    .out9(blt), .out10(bge), .out11(beq), .out12(bne), .out13(bez), .out14(bnz), .out15(call),
    .in(I_instruction), .sel(opcodeI));
  Multiplexer #(.width(16), .enable("false")) multiplexer_7 (
    .in0(multiplexer_5_out), .in1(Data2), .out(Go_B), .sel(ori));
  Extender extender_6 (.immediate(Data2), .\output (extender_6_output));
  Extender extender_7 (.immediate(Data2), .\output (extender_7_output));
  Extender extender_8 (.immediate(Data2), .\output (extender_8_output));
  Extender extender_9 (.immediate(Data2), .\output (extender_9_output));
  Shifter #(.width(16)) shifter_1 (.in(Data2), .\dist (4'b1000), .out(shifter_1_out));
  Multiplexer #(.width(16), .enable("false")) multiplexer_8 (.in0(Data3), .in1(rs_out), .out(Data4), .sel(mov));
  or or_2 (addF, add, mac, adi);
  or or_3 (shlF, shl, sli);
  Priority_Encoder priority_encoder_1 (
    .in0(1'b1), .in1(orF), .in2(\not ), .in3(addF), .in4(subF), .in5(mul), .in6(shlF), .in7(shrF),
    .out(Operation));  // open: en_in, gs, en_out
  Multiplexer #(.width(16), .enable("false")) multiplexer_9 (
    .in0(extender_7_output), .in1({16{1'b0}}), .out(bge_out), .sel(NF));
  Multiplexer #(.width(16), .enable("false")) multiplexer_10 (
    .in0({16{1'b0}}), .in1(extender_8_output), .out(beq_out), .sel(ZF));
  Comparator #(.width(16)) comparator_2 (
    .a(rs_out), .b({16{1'b0}}), .gt(comparator_2_gt), .lt(comparator_2_lt));  // open: eq
  or or_4 (or_4_out, comparator_2_gt, comparator_2_lt);
  assign or_5_out = shifter_1_out | rs_out;  // OR_Gate or_5, 16 bits wide
  Register #(.width(1)) register_1 (.D(Negative), .en(Flag_Enable), .Q(NF), .clk(CLK));  // open: clr
  Multiplexer #(.width(16), .enable("false")) multiplexer_11 (
    .in0({16{1'b0}}), .in1(extender_6_output), .out(blt_out), .sel(NF));
  Multiplexer #(.width(16), .enable("false")) multiplexer_12 (
    .in0({16{1'b0}}), .in1(extender_9_output), .out(bnz_out), .sel(or_4_out));
  Multiplexer #(.width(16), .enable("false")) multiplexer_13 (.in0(imm_t), .in1(or_5_out), .out(Data3), .sel(lui));
  or or_6 (Flag_Enable, add, sub, cmp, adi, cpi);
  Adder #(.width(32)) adder_1 (.a({m_high, m_low}), .b({m_high, m_low}), .out(mac_value));  // open: cin, cout
  Register #(.width(1)) register_2 (.D(zero), .en(Flag_Enable), .Q(ZF), .clk(CLK));  // open: clr
  or or_7 (andF, \and , ani);
  or or_8 (shrF, shr, sri);
  or or_9 (subF, sub, cpi, cmp);
  or or_10 (orF, \or , ori);
  or or_11 (decr7, push, call);
  or or_12 (incr7, pop, ret);
  Multiplexer #(.width(16), .enable("false")) multiplexer_14 (.in0(rt_out), .in1(Data2), .out(B_input), .sel(check_rt));
  or or_13 (check_rt, adi, ani, ori, sli, sri, cpi);
  Display_Unit display_unit_1 (.CLK(CLK), .Data(rs_out), .WE(put), .Clear(clr), ._4(_4), ._3(_3), ._2(_2), ._1(_1));
  Priority_Encoder #(.select(4)) priority_encoder_2 (
    .in0(li), .in1(lui), .in2(mov), .in3(ld), .in4(mfhi), .in5(mflo), .in6(andF), .in7(orF), .in8(\not ),
    .in9(addF), .in10(subF), .in11(mul), .in12(shlF), .in13(shrF), .in14(pop), .out(priority_encoder_2_out));  // open: in15, gs, en_out, en_in
  Multiplexer #(.select(4), .width(16), .enable("false")) multiplexer_15 (
    .in0(Data2), .in1(Data3), .in2(Data4), .in3(RAM), .in4(m_high), .in5(m_low), .in6(result), .in7(result),
    .in8(result), .in9(result), .in10(result), .in11(result), .in12(result), .in13(result), .in14(RAM),
    .out(multiplexer_15_out), .sel(priority_encoder_2_out));  // open: in15
  Multiplexer #(.width(16), .enable("false")) multiplexer_16 (
    .in0(multiplexer_15_out), .in1(rs_out), .out(multiplexer_16_out), .sel(cmp));
  Multiplexer #(.width(3), .enable("false")) multiplexer_17 (
    .in0(rd), .in1(3'b111), .out(multiplexer_17_out), .sel(call));
  or or_14 (or_14_out, push, pop, ret);
  Multiplexer #(.width(16), .enable("false")) multiplexer_18 (
    .in0(multiplexer_16_out), .in1(rs_out), .out(multiplexer_18_out), .sel(cpi));
  Multiplexer #(.width(3), .enable("false")) multiplexer_19 (
    .in0(rs), .in1(3'b111), .out(multiplexer_19_out), .sel(or_14_out));
  Register_file register_file_1 (
    .I_type(I_type), .CLK(CLK), .Data(multiplexer_18_out), .li(li), .rd(multiplexer_17_out),
    .rs(multiplexer_19_out), .rt(rt), .incr7(incr7), .decr7(decr7), .rs_out(rs_out), .rt_out(rt_out));
  or or_15 (or_15_out, bge, bnz, b, blt, beq, bne, bez, call);
  Multiplexer #(.width(16), .enable("false")) multiplexer_20 (
    .in0(RAM), .in1(rs_out), .out(multiplexer_20_out), .sel(jr));
  PC u_pc_1 (
    .Halt(halt), .CLK(CLK), .Jump_Choice(or_15_out), .Branch_Offset(PC_branchoffset), .ret(ret), .jr(jr),
    .Straight_target(multiplexer_20_out), .PC(pc), .PC_1(pc_1));
  Priority_Encoder #(.select(4)) priority_encoder_3 (
    .in0(1'b1), .in1(b), .in2(blt), .in3(bge), .in4(beq), .in5(bne), .in6(bez), .in7(bnz), .in8(call),
    .out(priority_encoder_3_out));  // open: in9, in10, in11, in12, in13, in14, in15, gs, en_out, en_in
  Multiplexer #(.select(4), .width(16), .enable("false")) multiplexer_21 (
    .in0({16{1'b0}}), .in1(b_out), .in2(blt_out), .in3(bge_out), .in4(beq_out), .in5(bne_out), .in6(bez_out),
    .in7(bnz_out), .in8(call_out), .out(PC_branchoffset), .sel(priority_encoder_3_out));  // open: in9, in10, in11, in12, in13, in14, in15

  // Other names for the same wires on the sheet: Product_register[31:0] = {m_high, m_low}; RAM_Value[15:0] = RAM
endmodule

// EXT
module Extender (
  input  [15:0] immediate,
  output [15:0] \output 
);

  wire comparator_1_eq;
  wire [7:0] negator_1_out;
  wire [15:0] bit_extender_1_out, negator_2_out;

  Negator negator_1 (.in(immediate[7:0]), .out(negator_1_out));
  assign bit_extender_1_out = {{8{1'b0}}, negator_1_out};  // Bit_Extender bit_extender_1
  Negator #(.width(16)) negator_2 (.in(bit_extender_1_out), .out(negator_2_out));
  Comparator #(.width(1)) comparator_1 (.a(immediate[7]), .b(1'b1), .eq(comparator_1_eq));  // open: gt, lt
  Multiplexer #(.width(16), .enable("false")) multiplexer_1 (
    .in0(immediate), .in1(negator_2_out), .out(\output ), .sel(comparator_1_eq));

  // Other names for the same wires on the sheet: imm[15:0] = immediate
endmodule

// ALU
module ALU_component (
  input  [15:0] A,
  input  [15:0] B,
  input  [2:0] Operation,
  input  mac,
  input  CLK,
  input  [31:0] mac_Value,
  output [15:0] High,
  output [31:0] Product_Register,
  output [15:0] Result,
  output Zero,
  output Negative
);

  wire comparator_1_eq, PR_enable, undriven;
  wire [15:0] Add, AND, Mult, NOT, OR, Shift_Left, Shift_Right, Sub, Upper_Bit_Mult;
  wire [31:0] bit_extender_1_out, bit_extender_2_out, PR_input, PR_input2, shifter_3_out;

  assign AND = A & B;  // AND_Gate and_1, 16 bits wide
  assign OR = A | B;  // OR_Gate or_1, 16 bits wide
  assign NOT = ~A;  // NOT_Gate not_1, 16 bits wide
  Adder #(.width(16)) adder_1 (.a(A), .b(B), .out(Add));  // open: cin, cout
  Subtractor #(.width(16)) subtractor_1 (.a(A), .b(B), .out(Sub));  // open: bin, bout
  Multiplier #(.width(16)) multiplier_1 (.a(A), .b(B), .out(Mult), .cout(Upper_Bit_Mult));  // open: cin
  Shifter #(.width(16)) shifter_1 (.in(A), .\dist (B[3:0]), .out(Shift_Left));
  Shifter #(.width(16), .shift("lr")) shifter_2 (.in(A), .\dist (B[3:0]), .out(Shift_Right));
  // Probe on A
  // Probe on Upper_Bit_Mult
  // Probe on B
  Comparator #(.width(3)) comparator_1 (.a(Operation), .b(3'b101), .eq(comparator_1_eq));  // open: gt, lt
  assign High = Upper_Bit_Mult & {16{1'b1}};  // AND_Gate and_2, 16 bits wide
  or or_2 (PR_enable, mac, comparator_1_eq);
  // Probe on undriven
  // Probe on Result
  Multiplexer #(.select(3), .width(16), .enable("false")) multiplexer_1 (
    .in0(AND), .in1(OR), .in2(NOT), .in3(Add), .in4(Sub), .in5(Mult), .in6(Shift_Left), .in7(Shift_Right),
    .out(Result), .sel(Operation));
  assign bit_extender_1_out = {{16{1'b0}}, High};  // Bit_Extender bit_extender_1
  assign bit_extender_2_out = {{16{1'b0}}, Mult};  // Bit_Extender bit_extender_2
  Comparator #(.width(16)) comparator_2 (.a(Result), .b({16{1'b0}}), .eq(Zero));  // open: gt, lt
  Comparator #(.width(16)) comparator_3 (.a(Result), .b({16{1'b0}}), .lt(Negative));  // open: gt, eq
  Shifter #(.width(32)) shifter_3 (.in(bit_extender_1_out), .\dist (5'b10000), .out(shifter_3_out));
  assign PR_input = shifter_3_out | bit_extender_2_out;  // OR_Gate or_3, 32 bits wide
  Multiplexer #(.width(32), .enable("false")) multiplexer_2 (
    .in0(PR_input), .in1(mac_Value), .out(PR_input2), .sel(mac));
  Register #(.width(32)) u_Product_register (
    .D(PR_input2), .en(PR_enable), .Q(Product_Register), .clk(CLK));  // open: clr
endmodule
